// Logisim project Catedra 4.circ as structural Verilog: 4 circuits, main circuit main
module main (
  input  X,
  output Y
);
endmodule

module Combinacional (
  input  in_1
);
endmodule

module d1 (
  input  X,
  input  Q0,
  input  Q1,
  output out_4
);

  wire and_1_out, and_2_out;

  and and_1 (and_1_out, X, Q0);
  or or_1 (out_4, and_1_out, and_2_out);
  and and_2 (and_2_out, X, Q1);
endmodule

module d0 (
  input  X,
  input  Q0,
  input  Q1,
  output out_4
);

  wire not_1_out, not_2_out;

  not not_1 (not_1_out, Q0);
  not not_2 (not_2_out, Q1);
  and and_1 (out_4, X, not_1_out, not_2_out);
endmodule
