// Logisim project Tarea 2.circ as structural Verilog: 2 circuits, main circuit DIVFREC_COMB
module DIVFREC (
  input  x1,
  input  x0,
  output clkout
);

  wire clock_1_out, divfrec_comb_1_d0, divfrec_comb_1_d1, register_1_q, register_2_q;

  Clock clock_1 (.out(clock_1_out));
  Register #(.width(1), .trigger("falling")) register_1 (
    .D(divfrec_comb_1_d1), .Q(register_1_q), .clk(clock_1_out));  // open: en, clr
  DIVFREC_COMB divfrec_comb_1 (
    .x1(x1), .x0(x0), .q1(register_1_q), .q0(register_2_q), .clkout(clkout), .d1(divfrec_comb_1_d1),
    .d0(divfrec_comb_1_d0));
  Register #(.width(1), .trigger("falling")) register_2 (
    .D(divfrec_comb_1_d0), .Q(register_2_q), .clk(clock_1_out));  // open: en, clr
endmodule

module DIVFREC_COMB (
  input  x1,
  input  x0,
  input  q1,
  input  q0,
  output clkout,
  output d1,
  output d0
);

  wire and_1_out, and_2_out, and_3_out, and_4_out, and_5_out, and_6_out, not_1_out, not_2_out, not_3_out,
       not_4_out;

  not not_1 (not_1_out, x1);
  not not_2 (not_2_out, x0);
  not not_3 (not_3_out, q1);
  not not_4 (not_4_out, q0);
  or or_1 (clkout, q1, and_1_out);
  and and_1 (and_1_out, q0, not_1_out, not_2_out);
  and and_2 (and_2_out, q0, x0);
  and and_3 (and_3_out, q1, not_4_out, x1);
  and and_4 (and_4_out, not_3_out, q0, x1);
  or or_2 (d1, and_2_out, and_4_out, and_3_out);
  and and_5 (and_5_out, not_3_out, not_4_out);
  and and_6 (and_6_out, not_4_out, x1);
  or or_3 (d0, and_5_out, and_6_out);
endmodule
