// Logisim project Tarea 3.circ as structural Verilog: 2 circuits, main circuit LOG 2
module LOG_2 (
  input  START,
  input  [7:0] D7_D0,
  input  CLK,
  output [2:0] Z2_Z0,
  output RDY,
  output ERR
);

  wire bitfinder_1_found, bitfinder_2_found, not_1_out;
  wire [2:0] adder_1_out, bit_extender_1_out, multiplexer_2_out;
  wire [7:0] D_q, multiplexer_1_out, shifter_1_out, shifter_2_out;

  BitFinder bitfinder_1 (.in(D7_D0), .found(bitfinder_1_found));  // open: index
  not not_1 (not_1_out, bitfinder_1_found);
  Multiplexer #(.width(8), .enable("false")) multiplexer_1 (
    .in0(shifter_2_out), .in1(shifter_1_out), .out(multiplexer_1_out), .sel(START));
  Shifter #(.shift("lr")) shifter_1 (.in(D7_D0), .\dist (3'b001), .out(shifter_1_out));
  Register #(.width(1), .trigger("falling")) u_ERR (.D(not_1_out), .Q(ERR), .clk(CLK));  // open: en, clr
  Multiplexer #(.width(3), .enable("false")) multiplexer_2 (
    .in0(adder_1_out), .in1(3'b000), .out(multiplexer_2_out), .sel(START));
  Register #(.width(3), .trigger("falling")) register_1 (.D(multiplexer_2_out), .Q(Z2_Z0), .clk(CLK));  // open: en, clr
  Register #(.trigger("falling")) D (.D(multiplexer_1_out), .Q(D_q), .clk(CLK));  // open: en, clr
  // Probe on D_q
  BitFinder bitfinder_2 (.in(D_q), .found(bitfinder_2_found));  // open: index
  assign bit_extender_1_out = {{2{1'b0}}, bitfinder_2_found};  // Bit_Extender bit_extender_1
  Adder #(.width(3)) adder_1 (.a(Z2_Z0), .b(bit_extender_1_out), .out(adder_1_out));  // open: cin, cout
  Shifter #(.shift("lr")) shifter_2 (.in(D_q), .\dist (3'b001), .out(shifter_2_out));
  nor nor_1 (RDY, D_q[0], D_q[1], D_q[2], D_q[3], D_q[4], D_q[5], D_q[6], D_q[7]);
endmodule

module other (
  input  START,
  input  [7:0] D7_D0,
  output [2:0] Z2_Z0,
  output RDY,
  output ERR
);

  wire clock_1_out;

  Clock clock_1 (.out(clock_1_out));
  LOG_2 LOG_2 (.START(START), .D7_D0(D7_D0), .CLK(clock_1_out), .Z2_Z0(Z2_Z0), .RDY(RDY), .ERR(ERR));
endmodule
