// Logisim project aux 2.circ as structural Verilog: 4 circuits, main circuit DETECTOR
module DETECTOR (
  input  X,
  input  Y,
  output ADEL,
  output ATRAS
);

  wire clock_1_out, det_comb_1_d0, det_comb_1_d1, Q0_q, Q1_q;

  Clock clock_1 (.out(clock_1_out));
  Register #(.width(1), .trigger("falling")) Q0 (.D(det_comb_1_d0), .Q(Q0_q), .clk(clock_1_out));  // open: en, clr
  DET_COMB det_comb_1 (
    .X(X), .Y(Y), .Q0(Q0_q), .Q1(Q1_q), .ADEL(ADEL), .ATRAS(ATRAS), .D0(det_comb_1_d0), .D1(det_comb_1_d1));
  Register #(.width(1), .trigger("falling")) Q1 (.D(det_comb_1_d1), .Q(Q1_q), .clk(clock_1_out));  // open: en, clr
endmodule

module DET_COMB (
  input  X,
  input  Y,
  input  Q0,
  input  Q1,
  output ADEL,
  output ATRAS,
  output D0,
  output D1
);

  ADEL adel_1 (.X(X), .Y(Y), .Q0(Q0), .Q1(Q1), .ADEL(ADEL));
  ATRAS atras_1 (.X(X), .Y(Y), .Q0(Q0), .Q1(Q1), .ATRAS(ATRAS));

  assign D0 = X;
  assign D1 = Y;
endmodule

module ADEL (
  input  X,
  input  Y,
  input  Q0,
  input  Q1,
  output ADEL
);

  wire and_1_out, and_2_out, and_3_out, and_4_out, not_1_out, not_2_out, not_3_out, not_4_out;

  not not_1 (not_1_out, X);
  not not_2 (not_2_out, Y);
  not not_3 (not_3_out, Q0);
  not not_4 (not_4_out, Q1);
  and and_1 (and_1_out, Q0, Q1, not_1_out);
  and and_2 (and_2_out, Q1, not_1_out, not_2_out);
  or or_1 (ADEL, and_1_out, and_2_out, and_3_out, and_4_out);
  and and_3 (and_3_out, not_3_out, X, not_2_out);
  and and_4 (and_4_out, Q0, not_4_out, Y);
endmodule

module ATRAS (
  input  X,
  input  Y,
  input  Q0,
  input  Q1,
  output ATRAS
);

  wire and_1_out, and_2_out, and_3_out, and_4_out, not_1_out, not_2_out, not_3_out, not_4_out;

  not not_1 (not_1_out, X);
  not not_2 (not_2_out, Y);
  not not_3 (not_3_out, Q0);
  not not_4 (not_4_out, Q1);
  and and_1 (and_1_out, Q0, not_1_out, not_2_out);
  and and_2 (and_2_out, not_3_out, X, Y);
  or or_1 (ATRAS, and_1_out, and_2_out, and_3_out, and_4_out);
  and and_3 (and_3_out, Q1, X, not_2_out);
  and and_4 (and_4_out, not_3_out, X, Y);
endmodule
