// Logisim project P1-terminada.circ as structural Verilog: 10 circuits, main circuit BCD
// A
module a (
  input  x0,
  input  x1,
  input  x2,
  input  x3,
  output a
);

  wire and_1_out, and_2_out, not_1_out, not_2_out;

  not not_1 (not_1_out, x0);
  not not_2 (not_2_out, x2);
  and and_1 (and_1_out, x0, x2);
  and and_2 (and_2_out, not_1_out, not_2_out);
  or or_1 (a, and_1_out, x1, and_2_out, x3);
endmodule

// B
module b (
  input  x0,
  input  x1,
  input  x2,
  input  x3,
  output b
);

  wire and_1_out, and_2_out, not_1_out, not_2_out, not_3_out;

  not not_1 (not_1_out, x0);
  not not_2 (not_2_out, x1);
  not not_3 (not_3_out, x2);
  and and_1 (and_1_out, x0, x1);
  and and_2 (and_2_out, not_1_out, not_2_out);
  or or_1 (b, and_1_out, and_2_out, not_3_out);
endmodule

// C
module c (
  input  x0,
  input  x1,
  input  x2,
  input  x3,
  output c
);

  wire not_1_out;

  not not_1 (not_1_out, x1);
  or or_1 (c, x0, not_1_out, x2);
endmodule

// D
module d (
  input  x0,
  input  x1,
  input  x2,
  input  x3,
  output d
);

  wire and_1_out, and_2_out, and_3_out, and_4_out, not_1_out, not_2_out, not_3_out;

  not not_1 (not_1_out, x1);
  not not_2 (not_2_out, x2);
  not not_3 (not_3_out, x0);
  and and_1 (and_1_out, not_3_out, x1);
  and and_2 (and_2_out, x1, not_2_out);
  and and_3 (and_3_out, not_3_out, not_2_out);
  and and_4 (and_4_out, x2, x0, not_1_out);
  or or_1 (d, and_1_out, and_2_out, and_3_out, and_4_out, x3);
endmodule

// E
module e (
  input  x0,
  input  x1,
  input  x2,
  input  x3,
  output e
);

  wire and_1_out, and_2_out, not_1_out, not_2_out;

  not not_1 (not_1_out, x0);
  not not_2 (not_2_out, x2);
  and and_1 (and_1_out, x1, not_1_out);
  and and_2 (and_2_out, not_1_out, not_2_out);
  or or_1 (e, and_1_out, and_2_out);
endmodule

// F
module f (
  input  x0,
  input  x1,
  input  x2,
  input  x3,
  output f
);

  wire and_1_out, and_2_out, and_3_out, and_4_out, not_1_out, not_2_out;

  not not_1 (not_1_out, x0);
  not not_2 (not_2_out, x1);
  and and_1 (and_1_out, not_1_out, not_2_out);
  and and_2 (and_2_out, not_1_out, x1, x2);
  and and_3 (and_3_out, x2, not_2_out);
  buf and_4 (and_4_out, x3);  // AND_Gate
  or or_1 (f, and_1_out, and_2_out, and_3_out, and_4_out);
endmodule

// G
module g (
  input  x0,
  input  x1,
  input  x2,
  input  x3,
  output g
);

  wire and_1_out, and_2_out, and_3_out, and_4_out, not_1_out, not_2_out, not_3_out;

  not not_1 (not_1_out, x0);
  not not_2 (not_2_out, x1);
  not not_3 (not_3_out, x2);
  and and_1 (and_1_out, not_1_out, x1);
  and and_2 (and_2_out, x1, not_3_out);
  and and_3 (and_3_out, not_2_out, x2);
  and and_4 (and_4_out, not_3_out, x3);
  or or_1 (g, and_1_out, and_2_out, and_3_out, and_4_out);
endmodule

module BCD (
  input  x0,
  input  x1,
  input  x2,
  input  x3,
  output a,
  output b,
  output c,
  output d,
  output e,
  output f,
  output g
);

  a a_1 (.x0(x0), .x1(x1), .x2(x2), .x3(x3), .a(a));
  b b_1 (.x0(x0), .x1(x1), .x2(x2), .x3(x3), .b(b));
  c c_1 (.x0(x0), .x1(x1), .x2(x2), .x3(x3), .c(c));
  d d_1 (.x0(x0), .x1(x1), .x2(x2), .x3(x3), .d(d));
  e e_1 (.x0(x0), .x1(x1), .x2(x2), .x3(x3), .e(e));
  f f_1 (.x0(x0), .x1(x1), .x2(x2), .x3(x3), .f(f));
  g g_1 (.x0(x0), .x1(x1), .x2(x2), .x3(x3), .g(g));
endmodule

module Prueba (
);

  wire bcd_1_a, bcd_1_d, bcd_1_g;
  wire [3:3] bcd_1_b, bcd_1_c, bcd_1_e, bcd_1_f;

  BCD bcd_1 (
    .x0(1'b1), .x1(1'b0), .x2(1'b0), .x3(1'b0), .a(bcd_1_a), .b(bcd_1_b[3]), .c(bcd_1_c[3]), .d(bcd_1_d),
    .e(bcd_1_e[3]), .f(bcd_1_f[3]), .g(bcd_1_g));
  DotMatrix #(.matrixcols(4), .matrixrows(1)) dotmatrix_1 (
    .col0(bcd_1_a), .col1(bcd_1_a), .col2(bcd_1_a), .col3(bcd_1_a));
  DotMatrix #(.matrixcols(1), .matrixrows(4)) dotmatrix_2 (.col0({4{bcd_1_f[3]}}));
  DotMatrix #(.matrixcols(4), .matrixrows(1)) dotmatrix_3 (
    .col0(bcd_1_g), .col1(bcd_1_g), .col2(bcd_1_g), .col3(bcd_1_g));
  DotMatrix #(.matrixcols(1), .matrixrows(4)) dotmatrix_4 (.col0({4{bcd_1_e[3]}}));
  DotMatrix #(.matrixcols(4), .matrixrows(1)) dotmatrix_5 (
    .col0(bcd_1_d), .col1(bcd_1_d), .col2(bcd_1_d), .col3(bcd_1_d));
  DotMatrix #(.matrixcols(1), .matrixrows(4)) dotmatrix_6 (.col0({4{bcd_1_b[3]}}));
  DotMatrix #(.matrixcols(1), .matrixrows(4)) dotmatrix_7 (.col0({4{bcd_1_c[3]}}));
endmodule

module Prueba2 (
  input  x0,
  input  x1,
  input  x2,
  input  x3
);

  wire bcd_1_a, bcd_1_b, bcd_1_c, bcd_1_d, bcd_1_e, bcd_1_f, bcd_1_g;

  BCD bcd_1 (
    .x0(x0), .x1(x1), .x2(x2), .x3(x3), .a(bcd_1_a), .b(bcd_1_b), .c(bcd_1_c), .d(bcd_1_d), .e(bcd_1_e),
    .f(bcd_1_f), .g(bcd_1_g));
  _7_Segment_Display u_7_segment_display_1 (
    .g(bcd_1_g), .f(bcd_1_f), .a(bcd_1_a), .b(bcd_1_b), .e(bcd_1_e), .d(bcd_1_d), .c(bcd_1_c));  // open: dp
endmodule
