// Logisim project Aux2P1.circ as structural Verilog: 5 circuits, main circuit DETECTOR
module DETECTOR (
  input  X,
  input  Y,
  output ADEL,
  output ATRAS
);

  wire clock_1_out, D0_Q0_q, D1_Q1_q, det_comb_1_d0, det_comb_1_d1;

  Clock clock_1 (.out(clock_1_out));
  DET_COMB det_comb_1 (
    .X(X), .Y(Y), .Q0(D0_Q0_q), .Q1(D1_Q1_q), .ADEL(ADEL), .ATRAS(ATRAS), .D0(det_comb_1_d0),
    .D1(det_comb_1_d1));
  Register #(.width(1), .trigger("falling")) D0_Q0 (
    .D(det_comb_1_d0), .Q(D0_Q0_q), .clk(clock_1_out));  // open: en, clr
  Register #(.width(1), .trigger("falling")) D1_Q1 (
    .D(det_comb_1_d1), .Q(D1_Q1_q), .clk(clock_1_out));  // open: en, clr
endmodule

module DET_COMB (
  input  X,
  input  Y,
  input  Q0,
  input  Q1,
  output ADEL,
  output ATRAS,
  output D0,
  output D1
);

  ADEL adel_1 (.X(X), .Y(Y), .Q0(Q0), .Q1(Q1), .ADEL(ADEL));
  ATRAS atras_1 (.X(X), .Y(Y), .Q0(Q0), .Q1(Q1), .ATRAS(ATRAS));

  assign D0 = X;
  assign D1 = Y;
endmodule

module ADEL (
  input  X,
  input  Y,
  input  Q0,
  input  Q1,
  output ADEL
);

  wire and_1_out, and_2_out, and_3_out, and_4_out, not_1_out, not_2_out, not_3_out, not_4_out;

  not not_1 (not_1_out, Q1);
  not not_2 (not_2_out, Y);
  not not_3 (not_3_out, Q0);
  not not_4 (not_4_out, X);
  and and_1 (and_1_out, Q0, Q1, not_4_out);
  and and_2 (and_2_out, Q1, not_4_out, not_2_out);
  and and_3 (and_3_out, not_3_out, X, not_2_out);
  and and_4 (and_4_out, Q0, not_1_out, Y);
  or or_1 (ADEL, and_1_out, and_2_out, and_3_out, and_4_out);

  // Notes on the sheet:
  //   ADEL = Q1~X~Y + Q0Q1~X + Q0~Q1Y+~Q0X~Y
endmodule

module ATRAS (
  input  X,
  input  Y,
  input  Q0,
  input  Q1,
  output ATRAS
);

  wire and_1_out, and_2_out, and_3_out, and_4_out, not_1_out, not_2_out, not_3_out, not_4_out;

  not not_1 (not_1_out, Q1);
  not not_2 (not_2_out, Y);
  not not_3 (not_3_out, Q0);
  not not_4 (not_4_out, X);
  and and_1 (and_1_out, not_3_out, not_1_out, Y);
  and and_2 (and_2_out, Q0, not_4_out, not_2_out);
  and and_3 (and_3_out, Q1, X, not_2_out);
  and and_4 (and_4_out, not_3_out, X, Y);
  or or_1 (ATRAS, and_1_out, and_2_out, and_3_out, and_4_out);

  // Notes on the sheet:
  //   ATRAS = ~Q0 ~Q1Y + ~Q0XY + Q1X~Y + Q0~X~Y
endmodule

module DETECTOR_V2 (
  input  X,
  input  Y,
  output ADEL,
  output ATRAS
);

  wire clock_1_out, D0_Q0_q, D1_Q1_q;

  // Probe on D0_Q0_q
  // Probe on D1_Q1_q
  Clock clock_1 (.out(clock_1_out));
  ADEL adel_1 (.X(X), .Y(Y), .Q0(D0_Q0_q), .Q1(D1_Q1_q), .ADEL(ADEL));
  ATRAS atras_1 (.X(X), .Y(Y), .Q0(D0_Q0_q), .Q1(D1_Q1_q), .ATRAS(ATRAS));
  Register #(.width(1), .trigger("falling")) D0_Q0 (.D(X), .Q(D0_Q0_q), .clk(clock_1_out));  // open: en, clr
  Register #(.width(1), .trigger("falling")) D1_Q1 (.D(Y), .Q(D1_Q1_q), .clk(clock_1_out));  // open: en, clr

  // Notes on the sheet:
  //   Q0
  //   Q1
endmodule
