// Logisim project FIB.circ as structural Verilog: 2 circuits, main circuit main
module main (
  input  reset,
  output [31:0] out_2
);

  wire clock_1_out;
  wire [31:0] adder_1_out, multiplexer_1_out, multiplexer_2_out, register_1_q;

  Adder #(.width(32)) adder_1 (.a(register_1_q), .b(out_2), .out(adder_1_out));  // open: cin, cout
  Multiplexer #(.width(32)) multiplexer_1 (
    .in0(adder_1_out), .in1(32'h1), .out(multiplexer_1_out), .sel(reset));  // open: en
  // Probe on multiplexer_1_out
  Register #(.width(32), .trigger("falling")) register_1 (
    .D(multiplexer_1_out), .Q(register_1_q), .clk(clock_1_out));  // open: en, clr
  Clock clock_1 (.out(clock_1_out));
  // Probe on multiplexer_2_out
  Multiplexer #(.width(32)) multiplexer_2 (
    .in0(register_1_q), .in1(32'h1), .out(multiplexer_2_out), .sel(reset));  // open: en
  Register #(.width(32), .trigger("falling")) register_2 (
    .D(multiplexer_2_out), .Q(out_2), .clk(clock_1_out));  // open: en, clr
  // Probe on out_2

  // Notes on the sheet:
  //   fn-2
  //   fn-1
endmodule

module fib_errorneo (
  input  reset,
  output [31:0] out_2
);

  wire clock_1_out, clock_2_out;
  wire [31:0] multiplexer_1_out, multiplexer_2_out, register_1_q, register_2_q;

  Multiplexer #(.width(32), .enable("false")) multiplexer_1 (
    .in0(out_2), .in1(32'h1), .out(multiplexer_1_out), .sel(reset));
  Multiplexer #(.width(32), .enable("false")) multiplexer_2 (
    .in0(register_1_q), .in1({32{1'b0}}), .out(multiplexer_2_out), .sel(reset));
  Register #(.width(32)) register_1 (.D(multiplexer_1_out), .Q(register_1_q), .clk(clock_1_out));  // open: en, clr
  Clock clock_1 (.out(clock_1_out));
  Register #(.width(32)) register_2 (.D(multiplexer_2_out), .Q(register_2_q), .clk(clock_2_out));  // open: en, clr
  Clock clock_2 (.out(clock_2_out));
  Adder #(.width(32)) adder_1 (.a(register_1_q), .b(register_2_q), .out(out_2));  // open: cin, cout
  // Probe on out_2

  // Notes on the sheet:
  //   fn-2
  //   fn-1
endmodule
