// Logisim project SEARCH.circ as structural Verilog: 1 circuit, main circuit main
module main (
  input  GT,
  input  EQ,
  input  START
);

  wire clock_1_out, clock_2_out;
  wire [7:0] adder_1_out, multiplexer_1_out, multiplexer_2_out, multiplexer_3_out, multiplexer_4_out,
       register_1_q, register_2_q, shifter_1_out, subtractor_1_out;

  Register #(.trigger("falling")) register_1 (
    .D(multiplexer_1_out), .Q(register_1_q), .clk(clock_1_out));  // open: en, clr
  Multiplexer #(.width(8)) multiplexer_1 (
    .in0(shifter_1_out), .in1(8'h80), .out(multiplexer_1_out), .sel(START));  // open: en
  Clock clock_1 (.out(clock_1_out));
  Subtractor subtractor_1 (.a(register_2_q), .b(shifter_1_out), .out(subtractor_1_out));  // open: bin, bout
  Adder adder_1 (.a(register_2_q), .b(shifter_1_out), .out(adder_1_out));  // open: cin, cout
  Shifter #(.shift("lr")) shifter_1 (.in(register_1_q), .\dist (3'b001), .out(shifter_1_out));
  Multiplexer #(.width(8)) multiplexer_2 (
    .in0(subtractor_1_out), .in1(adder_1_out), .out(multiplexer_2_out), .sel(GT));  // open: en
  Multiplexer #(.width(8)) multiplexer_3 (
    .in0(multiplexer_2_out), .in1(register_2_q), .out(multiplexer_3_out), .sel(EQ));  // open: en
  Multiplexer #(.width(8)) multiplexer_4 (
    .in0(multiplexer_3_out), .in1(8'h80), .out(multiplexer_4_out), .sel(START));  // open: en
  Register #(.trigger("falling")) register_2 (
    .D(multiplexer_4_out), .Q(register_2_q), .clk(clock_2_out));  // open: en, clr
  Clock clock_2 (.out(clock_2_out));
  // Probe on register_2_q
endmodule
