// Logisim project pauta_aux4.circ as structural Verilog: 4 circuits, main circuit main
module main (
  input  START,
  input  [3:0] X,
  input  [3:0] Y,
  output RDY,
  output [3:0] Z
);

  wire clock_1_out;

  Clock clock_1 (.out(clock_1_out));
  circuit part_1 (.START(START), .X(X), .Y(Y), .in_4(clock_1_out), .RDY(RDY), .out_6(Z));
endmodule

module RDY (
  input  CLK,
  input  START,
  output RDY
);

  wire [2:0] adder_1_out, I_q, multiplexer_1_out, multiplexer_2_out;

  Multiplexer #(.width(3), .enable("false")) multiplexer_1 (
    .in0(adder_1_out), .in1(I_q), .out(multiplexer_1_out), .sel(RDY));
  Multiplexer #(.width(3), .enable("false")) multiplexer_2 (
    .in0(multiplexer_1_out), .in1(3'b000), .out(multiplexer_2_out), .sel(START));
  Register #(.width(3), .trigger("falling")) I (.D(multiplexer_2_out), .Q(I_q), .clk(CLK));  // open: en, clr
  Adder #(.width(3)) adder_1 (.a(I_q), .b(3'b001), .out(adder_1_out));  // open: cin, cout
  Comparator #(.width(3)) comparator_1 (.a(adder_1_out), .b(3'b100), .eq(RDY));  // open: gt, lt
endmodule

module RDY2 (
  input  START,
  input  CLK,
  output RDY
);

  wire or_1_out;
  wire [3:0] multiplexer_1_out, register_1_q, shifter_1_out;

  Multiplexer #(.width(4), .enable("false")) multiplexer_1 (
    .in0(shifter_1_out), .in1(4'b1000), .out(multiplexer_1_out), .sel(START));
  // Probe on multiplexer_1_out
  Register #(.width(4), .trigger("falling")) register_1 (
    .D(multiplexer_1_out), .Q(register_1_q), .clk(CLK));  // open: en, clr
  Shifter #(.width(4), .shift("lr")) shifter_1 (.in(register_1_q), .\dist (2'b01), .out(shifter_1_out));
  or or_1 (or_1_out, shifter_1_out[0], shifter_1_out[1], shifter_1_out[2], shifter_1_out[3]);
  not not_1 (RDY, or_1_out);
endmodule

module circuit (
  input  START,
  input  [3:0] X,
  input  [3:0] Y,
  input  in_4,
  output RDY,
  output [3:0] out_6
);

  wire and_1_out, comparator_1_eq, comparator_1_gt, d_ff_1_q, not_1_out, or_1_out;
  wire [3:0] adder_1_out, multiplexer_3_out, multiplexer_6_out, shifter_2_out, z_correcto_q, Z_q;
  wire [7:0] _0X_q, bit_extender_1_out, bit_extender_2_out, multiplexer_1_out, multiplexer_2_out,
       multiplexer_5_out, shifter_1_out, shifter_3_out, subtractor_1_out, Y0_q;

  assign bit_extender_1_out = {{4{1'b0}}, X};  // Bit_Extender bit_extender_1
  assign bit_extender_2_out = {{4{1'b0}}, Y};  // Bit_Extender bit_extender_2
  Shifter shifter_1 (.in(bit_extender_2_out), .\dist (3'b100), .out(shifter_1_out));
  RDY rdy_1 (.START(START), .CLK(in_4), .RDY(RDY));
  Multiplexer #(.width(8), .enable("false")) multiplexer_1 (
    .in0(multiplexer_5_out), .in1(bit_extender_1_out), .out(multiplexer_1_out), .sel(START));
  Multiplexer #(.width(8), .enable("false")) multiplexer_2 (
    .in0(shifter_3_out), .in1(shifter_1_out), .out(multiplexer_2_out), .sel(START));
  Multiplexer #(.width(4), .enable("false")) multiplexer_3 (
    .in0(multiplexer_6_out), .in1(4'b0000), .out(multiplexer_3_out), .sel(START));
  Register #(.trigger("falling")) _0X (.D(multiplexer_1_out), .Q(_0X_q), .clk(in_4));  // open: en, clr
  Register #(.trigger("falling")) Y0 (.D(multiplexer_2_out), .Q(Y0_q), .clk(in_4));  // open: en, clr
  Register #(.width(4), .trigger("falling")) Z (.D(multiplexer_3_out), .Q(Z_q), .clk(in_4));  // open: en, clr
  // Probe on Z_q
  D_Flip_Flop #(.trigger("falling")) d_ff_1 (.clk(in_4), .D(RDY), .Q(d_ff_1_q));  // open: Qn, preset, en, reset
  // Probe on shifter_3_out
  // Probe on _0X_q
  Shifter #(.width(4)) shifter_2 (.in(Z_q), .\dist (2'b01), .out(shifter_2_out));
  Register #(.width(4), .trigger("falling")) z_correcto (.D(out_6), .Q(z_correcto_q), .clk(in_4));  // open: en, clr
  not not_1 (not_1_out, d_ff_1_q);
  Subtractor subtractor_1 (.a(_0X_q), .b(shifter_3_out), .out(subtractor_1_out));  // open: bin, bout
  Shifter #(.shift("lr")) shifter_3 (.in(Y0_q), .\dist (3'b001), .out(shifter_3_out));
  and and_1 (and_1_out, not_1_out, RDY);
  Adder #(.width(4)) adder_1 (.a(shifter_2_out), .b(4'b0001), .out(adder_1_out));  // open: cin, cout
  // Probe on multiplexer_6_out
  Multiplexer #(.width(4), .enable("false")) multiplexer_4 (
    .in0(z_correcto_q), .in1(multiplexer_6_out), .out(out_6), .sel(and_1_out));
  Multiplexer #(.width(8), .enable("false")) multiplexer_5 (
    .in0(_0X_q), .in1(subtractor_1_out), .out(multiplexer_5_out), .sel(or_1_out));
  Comparator comparator_1 (.a(_0X_q), .b(shifter_3_out), .gt(comparator_1_gt), .eq(comparator_1_eq));  // open: lt
  Multiplexer #(.width(4), .enable("false")) multiplexer_6 (
    .in0(shifter_2_out), .in1(adder_1_out), .out(multiplexer_6_out), .sel(or_1_out));
  or or_1 (or_1_out, comparator_1_gt, comparator_1_eq);
endmodule
